// Logisim project 1.circ as structural Verilog: 1 circuit, main circuit main
module main (
  input  A14,
  input  A15,
  input  IOREQ_high
);

  wire nor_1_out, nor_2_out, nor_3_out, nor_4_out, not_1_out;

  not not_1 (not_1_out, A14);
  nor nor_1 (nor_1_out, A14, 1'b0, 1'b0, A15, 1'b0);
  nor nor_2 (nor_2_out, 1'b0, 1'b0, A15, 1'b0, not_1_out);
  LED led_1 (.in(nor_3_out));
  nor nor_3 (nor_3_out, 1'b0, nor_1_out, 1'b0, IOREQ_high, 1'b0);
  nor nor_4 (nor_4_out, 1'b0, 1'b0, IOREQ_high, 1'b0, nor_2_out);
  LED led_2 (.in(nor_4_out));

  // Notes on the sheet:
  //   S1
  //   S0
endmodule
